// Digital circuit Projet2_Etape2.dig as structural Verilog
module Projet2_Etape2 (
  input  D,
  input  C,
  input  B,
  input  A,
  output S
);

  wire and_1_out, and_2_out, and_3_out;

  and and_1 (and_1_out, D, ~C, B, ~A);  // And
  and and_2 (and_2_out, D, C, B, A);
  and and_3 (and_3_out, ~D, C, ~B, A);  // And
  or or_1 (S, and_1_out, and_2_out, and_3_out);
endmodule
